// Logisim project dolezity_projekt_do__skoly.circ as structural Verilog: 1 circuit, main circuit main
module main (
  input  in_1,
  input  in_2,
  input  reset_memory,
  input  in_4,
  input  in_5,
  input  in_6,
  input  in_7
);

  wire and_1_out, and_2_out, and_4_out, clock_1_out, not_1_out, not_2_out, not_3_out, not_4_out, not_5_out,
       not_6_out, not_7_out, not_8_out, or_1_out, or_2_out, or_3_out, or_4_out, pull_resistor_5_node,
       pull_resistor_6_node, pull_resistor_7_node, pull_resistor_8_node, pull_resistor_9_node,
       pull_resistor_11_node, pull_resistor_13_node, pull_resistor_15_node, t_ff_2_q, t_ff_2_qn, t_ff_3_q,
       t_ff_3_qn, t_ff_4_q, t_ff_4_qn, t_ff_5_q, t_ff_5_qn, transistor_1_out, transistor_2_out,
       transistor_3_out, transistor_4_out, transistor_6_out, transistor_8_out, transistor_10_out,
       transistor_12_out, undriven, xor_1_out, xor_2_out, xor_3_out, xor_4_out, xor_5_out, xor_6_out,
       xor_7_out, xor_8_out;

  Clock clock_1 (.out(clock_1_out));
  not not_1 (not_1_out, clock_1_out);
  Transistor transistor_1 (.in(in_4), .out(transistor_1_out), .gate(reset_memory));
  Pull_Resistor pull_resistor_1 (.node(transistor_1_out));
  not not_2 (not_2_out, clock_1_out);
  Transistor transistor_2 (.in(in_5), .out(transistor_2_out), .gate(reset_memory));
  Pull_Resistor pull_resistor_2 (.node(transistor_2_out));
  not not_3 (not_3_out, clock_1_out);
  Transistor transistor_3 (.in(in_6), .out(transistor_3_out), .gate(reset_memory));
  Pull_Resistor pull_resistor_3 (.node(transistor_3_out));
  not not_4 (not_4_out, clock_1_out);
  Transistor transistor_4 (.in(in_7), .out(transistor_4_out), .gate(reset_memory));
  Pull_Resistor pull_resistor_4 (.node(transistor_4_out));
  Pull_Resistor pull_resistor_5 (.node(pull_resistor_5_node));
  Transistor transistor_5 (.in(or_1_out), .out(pull_resistor_5_node), .gate(not_1_out));
  or or_1 (or_1_out, pull_resistor_9_node, transistor_6_out);
  Transistor transistor_6 (.in(transistor_1_out), .out(transistor_6_out), .gate(not_5_out));
  Pull_Resistor pull_resistor_6 (.node(pull_resistor_6_node));
  Transistor transistor_7 (.in(or_2_out), .out(pull_resistor_6_node), .gate(not_2_out));
  or or_2 (or_2_out, pull_resistor_11_node, transistor_8_out);
  Transistor transistor_8 (.in(transistor_2_out), .out(transistor_8_out), .gate(not_6_out));
  Pull_Resistor pull_resistor_7 (.node(pull_resistor_7_node));
  Transistor transistor_9 (.in(or_3_out), .out(pull_resistor_7_node), .gate(not_3_out));
  or or_3 (or_3_out, pull_resistor_13_node, transistor_10_out);
  Transistor transistor_10 (.in(transistor_3_out), .out(transistor_10_out), .gate(not_7_out));
  Pull_Resistor pull_resistor_8 (.node(pull_resistor_8_node));
  Transistor transistor_11 (.in(or_4_out), .out(pull_resistor_8_node), .gate(not_4_out));
  or or_4 (or_4_out, pull_resistor_15_node, transistor_12_out);
  Transistor transistor_12 (.in(transistor_4_out), .out(transistor_12_out), .gate(not_8_out));
  T_Flip_Flop t_ff_1 (.T(undriven), .clk(undriven));  // open: Q, Qn, reset, preset
  Pull_Resistor pull_resistor_9 (.node(pull_resistor_9_node));
  Transistor transistor_13 (.in(reset_memory), .out(pull_resistor_9_node), .gate(t_ff_2_qn));
  Pull_Resistor pull_resistor_10 (.node(transistor_6_out));
  Pull_Resistor pull_resistor_11 (.node(pull_resistor_11_node));
  Transistor transistor_14 (.in(reset_memory), .out(pull_resistor_11_node), .gate(t_ff_3_qn));
  Pull_Resistor pull_resistor_12 (.node(transistor_8_out));
  Pull_Resistor pull_resistor_13 (.node(pull_resistor_13_node));
  Transistor transistor_15 (.in(reset_memory), .out(pull_resistor_13_node), .gate(t_ff_4_qn));
  Pull_Resistor pull_resistor_14 (.node(transistor_10_out));
  Pull_Resistor pull_resistor_15 (.node(pull_resistor_15_node));
  Transistor transistor_16 (.in(reset_memory), .out(pull_resistor_15_node), .gate(t_ff_5_qn));
  Pull_Resistor pull_resistor_16 (.node(transistor_12_out));
  T_Flip_Flop t_ff_2 (
    .T(clock_1_out), .clk(pull_resistor_5_node), .Q(t_ff_2_q), .Qn(t_ff_2_qn));  // open: reset, preset
  T_Flip_Flop t_ff_3 (
    .T(clock_1_out), .clk(pull_resistor_6_node), .Q(t_ff_3_q), .Qn(t_ff_3_qn));  // open: reset, preset
  T_Flip_Flop t_ff_4 (
    .T(clock_1_out), .clk(pull_resistor_7_node), .Q(t_ff_4_q), .Qn(t_ff_4_qn));  // open: reset, preset
  T_Flip_Flop t_ff_5 (
    .T(clock_1_out), .clk(pull_resistor_8_node), .Q(t_ff_5_q), .Qn(t_ff_5_qn));  // open: reset, preset
  not not_5 (not_5_out, t_ff_2_qn);
  not not_6 (not_6_out, t_ff_3_qn);
  not not_7 (not_7_out, t_ff_4_qn);
  not not_8 (not_8_out, t_ff_5_qn);
  buf xor_1 (xor_1_out, t_ff_2_q);  // XOR_Gate
  buf xor_2 (xor_2_out, t_ff_3_q);  // XOR_Gate
  buf xor_3 (xor_3_out, t_ff_4_q);  // XOR_Gate
  buf xor_4 (xor_4_out, t_ff_5_q);  // XOR_Gate
  and and_1 (and_1_out, and_4_out, xor_2_out);
  and and_2 (and_2_out, and_1_out, xor_3_out);
  // AND_Gate and_3 has open pins: in0=and_2_out, in1=xor_4_out, out=open
  xor xor_5 (xor_5_out, xor_1_out, in_2);
  and and_4 (and_4_out, in_2, xor_1_out);
  xor xor_6 (xor_6_out, xor_2_out, and_4_out);
  xor xor_7 (xor_7_out, xor_3_out, and_1_out);
  xor xor_8 (xor_8_out, xor_4_out, and_2_out);

  // Notes on the sheet:
  //   update clock
  //   hodně goofy 4 bit memory
  //   set memory
  //   W
  //   W
  //   W
  //   W
  //   R
  //   R
  //   R
  //   R
endmodule
